# Fritzing sketch LED and Buzzer (saved by Fritzing 0.9.3b)
breadboards: 1

parts:
  LED1 = LED - 3mm [color="Yellow (595nm)" package="3 mm [THT]"]
  R1 = Resistor [tolerance=±5% resistance=220 package="1206 [SMD]"]
  MCU1 = Raspberry Pi Zero
  LED2 = LED - 3mm [color="Green (570nm)" package="3 mm [THT]"]
  R2 = Resistor [tolerance=±5% resistance=220 package="1206 [SMD]"]
  LED3 = LED - 3mm [color="Red (633nm)" package="3 mm [THT]"]
  R3 = Resistor [tolerance=±5% resistance=220 package="1206 [SMD]"]
  J1 = Piezo Speaker

nets:
  N1: LED1.cathode, R1.Pin_1
  N2: LED1.anode, MCU1.pin_9, MCU1.pin_14, LED2.anode, LED3.anode, J1.pin1
  N3: R1.Pin_0, MCU1.pin_3
  N4: MCU1.pin_5, R2.Pin_0
  N5: MCU1.pin_7, R3.Pin_0
  N6: MCU1.pin_11, J1.pin2
  N7: LED2.cathode, R2.Pin_1
  N8: LED3.cathode, R3.Pin_1

notes:
  PIN OUT Description
  GPIO 2 - Yellow LED
  GPIO 3 - Green LED
  GPIO 4 - RED LED
  GPIO 17 - Buzzer
