# Fritzing sketch Simple LED Circuit (saved by Fritzing 0.9.3b)
breadboards: 1

parts:
  LED1 = LED - 3mm [color="Yellow (595nm)" package="3 mm [THT]"]
  R1 = Resistor [tolerance=±5% resistance=220 package="1206 [SMD]"]
  MCU1 = Raspberry Pi Zero

nets:
  N1: LED1.cathode, R1.Pin_1
  N2: LED1.anode, MCU1.pin_9
  N3: R1.Pin_0, MCU1.pin_3

notes:
  GPIO 2 - Yellow LED - OUT
